# Fritzing sketch pushbutton (saved by Fritzing 0.9.3b)
breadboards: 1

parts:
  Push = Momentary Switch [package=ksa_sealed_tac_switch]
  LED1 = LED - 5mm [color="Red (633nm)" package="5 mm [THT]"]
  R1 = Resistor [tolerance=±5% resistance=2.2k package=THT]
  R2 = Resistor [tolerance=±5% resistance=220 package=THT]
  WeMos_D1_Mini1 = WeMos D1 Mini

nets:
  N1: Push.2, R1.Pin_1, WeMos_D1_Mini1.D3
  N2: Push.4, LED1.cathode, WeMos_D1_Mini1.G
  N3: LED1.anode, R2.Pin_0
  N4: R1.Pin_0, WeMos_D1_Mini1.5V
  N5: R2.Pin_1, WeMos_D1_Mini1.D0
